// Logisim project a01_1.circ as structural Verilog: 1 circuit, main circuit main
module main (
  input  A,
  input  B,
  input  C,
  output P,
  output Q,
  output F,
  output R
);

  and and_1 (P, A, B);
  and and_2 (Q, B, C);
  and and_3 (R, C, A);
  or or_1 (F, P, Q, R);

  // Notes on the sheet:
  //   Dustin J Meckley
endmodule
