// Logisim project a01_2.circ as structural Verilog: 1 circuit, main circuit main
module main (
  input  X,
  input  Y,
  input  Z,
  output P,
  output Q,
  output R,
  output F
);

  not not_1 (P, X);
  nand nand_1 (Q, P, Y);
  nand nand_2 (R, X, Z);
  nand nand_3 (F, Q, R);

  // Notes on the sheet:
  //   Dustin J Meckley
endmodule
