// Logisim project a01_3.circ as structural Verilog: 1 circuit, main circuit main
module main (
  input  A,
  input  B,
  output P,
  output Q,
  output F
);

  or or_1 (P, A, B);
  nand nand_1 (Q, A, B);
  and and_1 (F, P, Q);

  // Notes on the sheet:
  //   Dustin J Meckley
endmodule
