// Logisim project a01_4.circ as structural Verilog: 1 circuit, main circuit main
// Y0
module main (
  input  X3,
  input  X2,
  input  X1,
  input  X0,
  output Y0,
  output Y1,
  output Y2,
  output Y3
);

  and and_1 (Y0, X0, ~X1, ~X2, ~X3);  // AND_Gate
  and and_2 (Y1, X1, ~X2, ~X3);  // AND_Gate
  and and_3 (Y2, X2, ~X3);  // AND_Gate

  assign Y3 = X3;

  // Notes on the sheet:
  //   Dustin J Meckley
endmodule
