// Logisim project a02_1.circ as structural Verilog: 2 circuits, main circuit main
module main (
);

  wire clock_1_out, decoder_1_a, decoder_1_b, decoder_1_c, decoder_1_d, decoder_1_e, decoder_1_f, decoder_1_g;
  wire [3:0] counter_1_q;

  Counter #(.width(4), .max('hf)) counter_1 (.Q(counter_1_q), .clk(clock_1_out));  // open: load, D, count, carry, clr
  Clock clock_1 (.out(clock_1_out));
  LED N2 (.in(counter_1_q[2]));
  LED N3 (.in(counter_1_q[3]));
  LED N1 (.in(counter_1_q[1]));
  LED N0 (.in(counter_1_q[0]));
  DECODER decoder_1 (
    .N0(counter_1_q[0]), .N1(counter_1_q[1]), .N2(counter_1_q[2]), .N3(counter_1_q[3]), .B(decoder_1_b),
    .D(decoder_1_d), .F(decoder_1_f), .A(decoder_1_a), .C(decoder_1_c), .E(decoder_1_e), .G(decoder_1_g));
  _7_Segment_Display u_7_segment_display_1 (
    .g(decoder_1_g), .f(decoder_1_f), .a(decoder_1_a), .b(decoder_1_b), .e(decoder_1_e), .d(decoder_1_d),
    .c(decoder_1_c));  // open: dp

  // Notes on the sheet:
  //   Dustin J Meckley
endmodule

module DECODER (
  input  N0,
  input  N1,
  input  N2,
  input  N3,
  output A,
  output B,
  output C,
  output D,
  output E,
  output F,
  output G
);

  wire and_1_out, and_2_out, and_3_out, and_4_out, and_5_out, and_6_out, and_7_out, and_8_out, and_9_out,
       and_10_out, and_11_out, and_12_out, and_13_out, and_14_out, and_15_out, and_16_out, and_17_out,
       and_18_out, and_19_out, and_20_out, and_21_out, and_22_out, and_23_out, and_24_out, and_25_out,
       and_26_out, and_27_out, and_28_out, and_29_out, and_30_out, and_31_out, and_32_out, and_33_out,
       and_34_out, and_35_out, and_36_out, and_37_out, and_38_out, and_39_out;

  and and_1 (and_1_out, ~N2, ~N0);  // AND_Gate
  and and_2 (and_2_out, ~N3, N2);  // AND_Gate
  and and_3 (and_3_out, ~N2, ~N0);  // AND_Gate
  and and_4 (and_4_out, N3, ~N2);  // AND_Gate
  and and_5 (and_5_out, N2, N1);
  and and_6 (and_6_out, N1, ~N0);  // AND_Gate
  and and_7 (and_7_out, N3, ~N2);  // AND_Gate
  and and_8 (and_8_out, N3, N2);
  and and_9 (and_9_out, N3, N1);
  and and_10 (and_10_out, ~N2, N1);  // AND_Gate
  and and_11 (and_11_out, ~N3, N1);  // AND_Gate
  and and_12 (and_12_out, ~N3, N0);  // AND_Gate
  and and_13 (and_13_out, ~N2, ~N1);  // AND_Gate
  and and_14 (and_14_out, N3, N1, N0);
  and and_15 (and_15_out, N1, ~N0);  // AND_Gate
  and and_16 (and_16_out, N3, N0);
  and and_17 (and_17_out, N3, N2, ~N0);  // AND_Gate
  and and_18 (and_18_out, ~N1, N0);  // AND_Gate
  and and_19 (and_19_out, N1, ~N0);  // AND_Gate
  and and_20 (and_20_out, N3, ~N2, ~N1);  // AND_Gate
  and and_21 (and_21_out, ~N3, N2, N0);  // AND_Gate
  and and_22 (and_22_out, ~N3, N2, ~N0);  // AND_Gate
  and and_23 (and_23_out, ~N3, N2, ~N1);  // AND_Gate
  or or_1 (E, and_14_out, and_15_out, and_8_out, and_3_out);
  or or_2 (A, and_20_out, and_21_out, and_17_out, and_11_out, and_5_out, and_6_out, and_1_out);
  or or_3 (C, and_18_out, and_12_out, and_13_out, and_7_out, and_2_out);
  or or_4 (D, and_25_out, and_28_out, and_29_out, and_34_out, and_37_out);
  or or_5 (F, and_26_out, and_30_out, and_31_out, and_35_out, and_38_out);
  or or_6 (G, and_23_out, and_22_out, and_19_out, and_16_out, and_9_out, and_10_out, and_4_out);
  or or_7 (B, and_24_out, and_27_out, and_33_out, and_32_out, and_36_out, and_39_out);
  and and_24 (and_24_out, ~N2, ~N0);  // AND_Gate
  and and_25 (and_25_out, N3, ~N1);  // AND_Gate
  and and_26 (and_26_out, N3, ~N2);  // AND_Gate
  and and_27 (and_27_out, ~N2, ~N1);  // AND_Gate
  and and_28 (and_28_out, ~N2, N1, N0);  // AND_Gate
  and and_29 (and_29_out, ~N3, ~N2, ~N0);  // AND_Gate
  and and_30 (and_30_out, ~N1, ~N0);  // AND_Gate
  and and_31 (and_31_out, N2, ~N0);  // AND_Gate
  and and_32 (and_32_out, ~N3, N1, N0);  // AND_Gate
  and and_33 (and_33_out, ~N3, ~N2);  // AND_Gate
  and and_34 (and_34_out, N2, N1, ~N0);  // AND_Gate
  and and_35 (and_35_out, N3, N1);
  and and_36 (and_36_out, ~N3, ~N1, ~N0);  // AND_Gate
  and and_37 (and_37_out, N2, ~N1, N0);  // AND_Gate
  and and_38 (and_38_out, ~N3, N2, ~N1);  // AND_Gate
  and and_39 (and_39_out, N3, ~N1, N0);  // AND_Gate

  // Notes on the sheet:
  //   N0
endmodule
