// Logisim project a03_1.circ as structural Verilog: 1 circuit, main circuit main
module main (
  input  COUNT,
  input  RESET,
  output Q1,
  output O2,
  output O3
);

  wire CLOCK_out, nN__nQ1_N_out, nQ1_N_out, nQ1_Q3_out, Q2_Q3__N_out, Q2_Q3_out, Q3_nN___nQ1Q3_out, Q3_nN_out;

  and Q3_nN (Q3_nN_out, O3, ~COUNT);  // AND_Gate
  and nQ1_Q3 (nQ1_Q3_out, ~Q1, O3);  // AND_Gate
  or Q3_nN___nQ1Q3 (Q3_nN___nQ1Q3_out, Q3_nN_out, nQ1_Q3_out);
  or nN__nQ1_N (nN__nQ1_N_out, ~COUNT, nQ1_N_out);  // OR_Gate
  and Q2_Q3 (Q2_Q3_out, O2, O3);
  or Q2_Q3__N (Q2_Q3__N_out, COUNT, Q2_Q3_out);
  Clock CLOCK (.out(CLOCK_out));
  J_K_Flip_Flop JK1 (.J(Q2_Q3_out), .clk(CLOCK_out), .K(Q2_Q3__N_out), .Q(Q1), .reset(RESET));  // open: Qn, preset, en
  J_K_Flip_Flop JK2 (
    .J(Q3_nN___nQ1Q3_out), .clk(CLOCK_out), .K(Q3_nN___nQ1Q3_out), .Q(O2), .reset(RESET));  // open: Qn, preset, en
  J_K_Flip_Flop JK3 (
    .J(nN__nQ1_N_out), .clk(CLOCK_out), .K(nN__nQ1_N_out), .Q(O3), .reset(RESET));  // open: Qn, preset, en
  and nQ1_N (nQ1_N_out, COUNT, ~Q1);  // AND_Gate

  // Notes on the sheet:
  //   Dustin Meckley - CISS420 Part 1 
endmodule
