// Logisim project a03_2.circ as structural Verilog: 2 circuits, main circuit main
module main (
);

  wire CLOCK_out, RESET_out;
  wire [3:0] RIGHT_out;
  wire [15:0] logic_1_output;

  Button LEFT (.out(RIGHT_out[3]));
  Clock CLOCK (.out(CLOCK_out));
  Button RESET (.out(RESET_out));
  Button UP (.out(RIGHT_out[1]));
  Button RIGHT (.out(RIGHT_out[0]));
  Button DOWN (.out(RIGHT_out[2]));
  \logic  logic_1 (.BUTTONS(RIGHT_out), .CLOCK(CLOCK_out), .RESET(RESET_out), .OUTPUT(logic_1_output));
  DotMatrix #(.inputtype("row"), .matrixcols(4), .matrixrows(4)) dotmatrix_1 (
    .row0(logic_1_output[3:0]), .row1(logic_1_output[7:4]), .row2(logic_1_output[11:8]),
    .row3(logic_1_output[15:12]));

  // Notes on the sheet:
  //   Dustin Meckley - CISS420 Part 2
endmodule

module \logic  (
  input  [3:0] BUTTONS,
  input  CLOCK,
  input  RESET,
  output [15:0] OUTPUT
);

  wire and_1_out, and_2_out, and_3_out, and_4_out, and_5_out, and_6_out, and_7_out, and_8_out, and_9_out,
       and_10_out, and_11_out, and_12_out, or_1_out, or_2_out, or_3_out, or_4_out;

  and and_1 (and_1_out, OUTPUT[4], BUTTONS[0]);
  and and_2 (and_2_out, BUTTONS[0], ~BUTTONS[3], ~OUTPUT[4]);  // AND_Gate
  and and_3 (and_3_out, BUTTONS[3], ~BUTTONS[0]);  // AND_Gate
  and and_4 (and_4_out, BUTTONS[0], ~BUTTONS[3], OUTPUT[0]);  // AND_Gate
  and and_5 (and_5_out, ~BUTTONS[3], BUTTONS[0]);  // AND_Gate
  and and_6 (and_6_out, ~BUTTONS[0], BUTTONS[3], ~OUTPUT[0]);  // AND_Gate
  and and_7 (and_7_out, OUTPUT[12], BUTTONS[1], ~BUTTONS[2]);  // AND_Gate
  and and_8 (and_8_out, ~OUTPUT[12], ~BUTTONS[1], BUTTONS[2]);  // AND_Gate
  and and_9 (and_9_out, BUTTONS[1], ~BUTTONS[2]);  // AND_Gate
  and and_10 (and_10_out, OUTPUT[8], ~BUTTONS[1], BUTTONS[2]);  // AND_Gate
  and and_11 (and_11_out, ~BUTTONS[1], BUTTONS[2]);  // AND_Gate
  and and_12 (and_12_out, ~OUTPUT[8], BUTTONS[1], ~BUTTONS[2]);  // AND_Gate
  J_K_Flip_Flop LR_JK1 (
    .J(and_1_out), .clk(CLOCK), .K(and_2_out), .Q(OUTPUT[0]), .reset(RESET));  // open: Qn, preset, en
  or or_1 (or_1_out, and_3_out, and_4_out);
  or or_2 (or_2_out, and_5_out, and_6_out);
  J_K_Flip_Flop UD_JK1 (
    .J(and_7_out), .clk(CLOCK), .K(and_8_out), .Q(OUTPUT[8]), .preset(RESET));  // open: Qn, en, reset
  or or_3 (or_3_out, and_9_out, and_10_out);
  or or_4 (or_4_out, and_11_out, and_12_out);
  J_K_Flip_Flop LR_JK0 (.J(or_1_out), .clk(CLOCK), .K(or_2_out), .Q(OUTPUT[4]), .reset(RESET));  // open: Qn, preset, en
  J_K_Flip_Flop UD_JK0 (
    .J(or_3_out), .clk(CLOCK), .K(or_4_out), .Q(OUTPUT[12]), .preset(RESET));  // open: Qn, en, reset
  // Pins of 1 and 4 bits meet at {3'b111, OUTPUT[4]}
  // Pins of 1 and 4 bits meet at {3'b111, OUTPUT[0]}
  // Pins of 1 and 4 bits meet at {3'b111, OUTPUT[12]}
  // Pins of 1 and 4 bits meet at {3'b111, OUTPUT[8]}

  assign {OUTPUT[15:13], OUTPUT[11:9], OUTPUT[7:5], OUTPUT[3:1]} = {12{1'b1}};
  // also tied to VCC on the sheet: {OUTPUT[0], OUTPUT[4], OUTPUT[8], OUTPUT[12]}

  // Notes on the sheet:
  //   Dustin Meckley - CISS420
endmodule
