// Logisim project control.circ as structural Verilog: 1 circuit, main circuit control
// Control
module control (
  input  [15:0] instruction,
  input  AC_Zero,
  input  AC_Negative,
  output PC_1,
  output [2:0] Read_From_ID,
  output [2:0] Write_To_ID,
  output [1:0] ALU_Function
);

  wire and_1_out, and_2_out, and_3_out, and_4_out, and_5_out, clock_1_out, clock_2_out, comparator_1_eq,
       comparator_2_eq, comparator_3_eq, Fetch_Execute_q, not_1_out, or_1_out;
  wire [1:0] Step_q;
  wire [10:0] rom_1_data, rom_2_data;
  wire [10:8] multiplexer_1_out;

  not not_1 (not_1_out, multiplexer_1_out[10]);
  Counter #(.width(2), .max('h3)) Step (
    .load(multiplexer_1_out[10]), .D(2'b00), .count(not_1_out), .Q(Step_q), .clk(clock_1_out));  // open: carry, clr
  Clock clock_1 (.out(clock_1_out));
  // Probe on {instruction[15:12], Step_q}
  Comparator #(.width(2)) comparator_1 (.a(instruction[11:10]), .b(2'b00), .eq(comparator_1_eq));  // open: gt, lt
  Comparator #(.width(2)) comparator_2 (.a(instruction[11:10]), .b(2'b01), .eq(comparator_2_eq));  // open: gt, lt
  Comparator #(.width(2)) comparator_3 (.a(instruction[11:10]), .b(2'b10), .eq(comparator_3_eq));  // open: gt, lt
  and and_1 (and_1_out, AC_Negative, AC_Zero);
  and and_2 (and_2_out, comparator_1_eq, AC_Negative);
  and and_3 (and_3_out, comparator_2_eq, AC_Zero);
  and and_4 (and_4_out, comparator_3_eq, and_1_out);
  Clock clock_2 (.out(clock_2_out));
  ROM #(.addrWidth(2), .dataWidth(11)) rom_1 (.addr(Step_q), .data(rom_1_data));  // open: sel
  ROM #(.addrWidth(6), .dataWidth(11)) rom_2 (.addr({instruction[15:12], Step_q}), .data(rom_2_data));  // open: sel
  or or_1 (or_1_out, and_2_out, and_3_out, and_4_out);
  T_Flip_Flop Fetch_Execute (
    .clk(clock_2_out), .T(multiplexer_1_out[10]), .Q(Fetch_Execute_q));  // open: Qn, preset, reset, en
  and and_5 (and_5_out, multiplexer_1_out[9], or_1_out);
  Multiplexer #(.width(11), .enable("false")) multiplexer_1 (
    .in0(rom_1_data), .in1(rom_2_data), .out({multiplexer_1_out, Read_From_ID, Write_To_ID, ALU_Function}),
    .sel(Fetch_Execute_q));
  or or_2 (PC_1, multiplexer_1_out[8], and_5_out);

  // Notes on the sheet:
  //   Fetch Micro-Ops
  //   Instruction Micro-Ops
  //   contents of rom_1 (hex, n*v repeats v):
  //   44 1c 548
  //   contents of rom_2 (hex, n*v repeats v):
  //   e4 40 e8 548 e4 410 0 0 e4 8c 460 0 e4 c 491 0 e4 c 492 0 4b0 0 0 0 498 7*0 748 448 0 0 4e8 0 0 0
  //   473 0 0 0 e4 4 c 491 e4 c 468 0 ec 4 c 470 ec 4 480
endmodule
