// Logisim project part_1_solution.circ as structural Verilog: 2 circuits, main circuit main
module main (
  input  [2:0] Write_Control,
  input  [2:0] Read_Control,
  output [15:0] Data_Bus
);

  wire busif_1_read_enable, busif_2_read_enable, busif_3_read_enable, clock_1_out;
  wire [15:0] busif_1_if_to_reg, busif_2_if_to_reg, busif_3_if_to_reg, register_1_q, register_2_q,
       register_3_q;

  Clock clock_1 (.out(clock_1_out));
  busif busif_1 (
    .Bus_ID(3'b000), .Bus_Write(Write_Control), .Bus_Read(Read_Control), .Bus_to_IF(Data_Bus),
    .Reg_to_IF(register_1_q), .IF_to_Reg(busif_1_if_to_reg), .Read_Enable(busif_1_read_enable),
    .IF_to_Bus(Data_Bus));
  busif busif_2 (
    .Bus_ID(3'b001), .Bus_Write(Write_Control), .Bus_Read(Read_Control), .Bus_to_IF(Data_Bus),
    .Reg_to_IF(register_2_q), .IF_to_Reg(busif_2_if_to_reg), .Read_Enable(busif_2_read_enable),
    .IF_to_Bus(Data_Bus));
  Register #(.width(16)) register_1 (
    .D(busif_1_if_to_reg), .en(busif_1_read_enable), .Q(register_1_q), .clk(clock_1_out));  // open: clr
  Register #(.width(16)) register_2 (
    .D(busif_2_if_to_reg), .en(busif_2_read_enable), .Q(register_2_q), .clk(clock_1_out));  // open: clr
  busif busif_3 (
    .Bus_ID(3'b010), .Bus_Write(Write_Control), .Bus_Read(Read_Control), .Bus_to_IF(Data_Bus),
    .Reg_to_IF(register_3_q), .IF_to_Reg(busif_3_if_to_reg), .Read_Enable(busif_3_read_enable),
    .IF_to_Bus(Data_Bus));
  Register #(.width(16)) register_3 (
    .D(busif_3_if_to_reg), .en(busif_3_read_enable), .Q(register_3_q), .clk(clock_1_out));  // open: clr

  // Notes on the sheet:
  //   MARIE Architecture Part 1
  //   Your Names Here
endmodule

module busif (
  input  [15:0] Bus_to_IF,
  input  [2:0] Bus_ID,
  input  [2:0] Bus_Write,
  input  [2:0] Bus_Read,
  input  [15:0] Reg_to_IF,
  output [15:0] IF_to_Bus,
  output [15:0] IF_to_Reg,
  output Read_Enable
);

  wire comparator_2_eq;

  Comparator #(.width(3)) comparator_1 (.a(Bus_ID), .b(Bus_Write), .eq(Read_Enable));  // open: gt, lt
  assign IF_to_Bus = comparator_2_eq ? Reg_to_IF : 16'bz;  // Controlled_Buffer controlled_buffer_1
  Comparator #(.width(3)) comparator_2 (.a(Bus_ID), .b(Bus_Read), .eq(comparator_2_eq));  // open: gt, lt

  assign IF_to_Reg = Bus_to_IF;
endmodule
