// Logisim project part_2.circ as structural Verilog: 3 circuits, main circuit main
module main (
  input  [2:0] Write_Control,
  input  [2:0] Read_Control,
  input  [1:0] F,
  output [15:0] Data_Bus,
  output [15:0] Q
);

  wire busif_1_read_enable, busif_2_read_enable, busif_3_read_enable, busif_4_read_enable,
       busif_5_read_enable, clock_1_out;
  wire [11:0] bit_extender_1_out, MAR_q;
  wire [15:0] AC_q, bit_extender_2_out, busif_1_if_to_reg, busif_2_if_to_reg, busif_3_if_to_reg,
       busif_4_if_to_reg, busif_5_if_to_reg, MBR_q, PC_q, ram_1_data;

  Clock clock_1 (.out(clock_1_out));
  busif busif_1 (
    .Bus_ID(3'b000), .Bus_Read(Read_Control), .Bus_to_IF(Data_Bus), .Reg_to_IF(ram_1_data),
    .IF_to_Reg(busif_1_if_to_reg), .Read_Enable(busif_1_read_enable), .IF_to_Bus(Data_Bus),
    .Bus_Write(Write_Control));
  RAM #(.addrWidth(12), .dataWidth(16), .bus("separate")) ram_1 (
    .addr(MAR_q), .din(busif_1_if_to_reg), .data(ram_1_data), .str(busif_1_read_enable), .clk(clock_1_out));  // open: sel, ld, clr
  busif busif_2 (
    .Bus_ID(3'b001), .Bus_Read(Read_Control), .Bus_to_IF(Data_Bus), .Reg_to_IF(bit_extender_2_out),
    .IF_to_Reg(busif_2_if_to_reg), .Read_Enable(busif_2_read_enable), .IF_to_Bus(Data_Bus),
    .Bus_Write(Write_Control));
  Register #(.width(12)) MAR (
    .D(bit_extender_1_out), .en(busif_2_read_enable), .Q(MAR_q), .clk(clock_1_out));  // open: clr
  Bit_Extender #(.in_width(16), .out_width(12)) bit_extender_1 (.in(busif_2_if_to_reg), .out(bit_extender_1_out));
  busif busif_3 (
    .Bus_ID(3'b010), .Bus_Read(Read_Control), .Bus_to_IF(Data_Bus), .Reg_to_IF(PC_q),
    .IF_to_Reg(busif_3_if_to_reg), .Read_Enable(busif_3_read_enable), .IF_to_Bus(Data_Bus),
    .Bus_Write(Write_Control));
  assign bit_extender_2_out = {{4{1'b0}}, MAR_q};  // Bit_Extender bit_extender_2
  busif busif_4 (
    .Bus_ID(3'b011), .Bus_Read(Read_Control), .Bus_to_IF(Data_Bus), .Reg_to_IF(MBR_q),
    .IF_to_Reg(busif_4_if_to_reg), .Read_Enable(busif_4_read_enable), .IF_to_Bus(Data_Bus),
    .Bus_Write(Write_Control));
  Register #(.width(16)) PC (
    .D(busif_3_if_to_reg), .en(busif_3_read_enable), .Q(PC_q), .clk(clock_1_out));  // open: clr
  Register #(.width(16)) MBR (
    .D(busif_4_if_to_reg), .en(busif_4_read_enable), .Q(MBR_q), .clk(clock_1_out));  // open: clr
  busif busif_5 (
    .Bus_ID(3'b100), .Bus_Read(Read_Control), .Bus_to_IF(Data_Bus), .Reg_to_IF(AC_q),
    .IF_to_Reg(busif_5_if_to_reg), .Read_Enable(busif_5_read_enable), .IF_to_Bus(Data_Bus),
    .Bus_Write(Write_Control));
  Register #(.width(16)) AC (
    .D(busif_5_if_to_reg), .en(busif_5_read_enable), .Q(AC_q), .clk(clock_1_out));  // open: clr
  ALU alu_1 (.A(AC_q), .B(MBR_q), .F(F), .Q(Q));

  // Notes on the sheet:
  //   MARIE Architecture Part 1
  //   Dustin Meckley
endmodule

module busif (
  input  [15:0] Bus_to_IF,
  input  [2:0] Bus_ID,
  input  [2:0] Bus_Write,
  input  [2:0] Bus_Read,
  input  [15:0] Reg_to_IF,
  output [15:0] IF_to_Bus,
  output [15:0] IF_to_Reg,
  output Read_Enable
);

  wire comparator_2_eq;

  Comparator #(.width(3)) comparator_1 (.a(Bus_ID), .b(Bus_Write), .eq(Read_Enable));  // open: gt, lt
  assign IF_to_Bus = comparator_2_eq ? Reg_to_IF : 16'bz;  // Controlled_Buffer controlled_buffer_1
  Comparator #(.width(3)) comparator_2 (.a(Bus_ID), .b(Bus_Read), .eq(comparator_2_eq));  // open: gt, lt

  assign IF_to_Reg = Bus_to_IF;

  // Notes on the sheet:
  //   P5 P4 P3
  //   P2 P1 P0
endmodule

module ALU (
  input  [15:0] A,
  input  [15:0] B,
  input  [1:0] F,
  output [15:0] Q
);

  wire [15:0] adder_1_out, subtractor_1_out;

  Adder #(.width(16)) adder_1 (.a(A), .b(B), .out(adder_1_out));  // open: cin, cout
  Subtractor #(.width(16)) subtractor_1 (.a(A), .b(B), .out(subtractor_1_out));  // open: bin, bout
  Multiplexer #(.select(2), .width(16), .enable("false")) multiplexer_1 (
    .in1(subtractor_1_out), .in2(adder_1_out), .in3({16{1'b0}}), .out(Q), .sel(F));  // open: in0

  // Notes on the sheet:
  //   A0 A1
  //   0   0   Do Nothing
  //   0   1   AC = AC - MBR
  //   1   0   AC = AC + MBR
  //   1   1   AC = 0 (Clear)
endmodule
