// Logisim project part_2_solution.circ as structural Verilog: 4 circuits, main circuit busif
// ALU
module main (
  input  [2:0] Write_To_ID,
  input  [2:0] Read_From_ID,
  input  [1:0] ALU_Func,
  output [15:0] Data_Bus,
  output [15:0] ALU_Output
);

  wire busif_1_read_enable, busif_2_read_enable, busif_3_read_enable, busif_4_read_enable, clock_1_out;
  wire [11:0] MAR_q, tiny_bit_extender_1__12b_to_reg;
  wire [15:0] AC_q, busif_1_if_to_reg, busif_2_if_to_reg, busif_3_if_to_reg, busif_4_if_to_reg, MBR_q,
       ram_1_data, tiny_bit_extender_1__16b_to_bus;

  Clock clock_1 (.out(clock_1_out));
  alu alu_1 (.A(AC_q), .B(MBR_q), .Q(ALU_Output), .F(ALU_Func));
  busif busif_1 (
    .Bus_ID(3'b100), .Bus_Write_to_ID(Write_To_ID), .Bus_Read_from_ID(Read_From_ID), .Bus_to_IF(Data_Bus),
    .Reg_to_IF(AC_q), .IF_to_Reg(busif_1_if_to_reg), .Read_Enable(busif_1_read_enable), .IF_to_Bus(Data_Bus));
  busif busif_2 (
    .Bus_ID(3'b011), .Bus_Write_to_ID(Write_To_ID), .Bus_Read_from_ID(Read_From_ID), .Bus_to_IF(Data_Bus),
    .Reg_to_IF(MBR_q), .IF_to_Reg(busif_2_if_to_reg), .Read_Enable(busif_2_read_enable), .IF_to_Bus(Data_Bus));
  Register #(.width(16)) AC (
    .D(busif_1_if_to_reg), .en(busif_1_read_enable), .Q(AC_q), .clk(clock_1_out));  // open: clr
  Register #(.width(16)) MBR (
    .D(busif_2_if_to_reg), .en(busif_2_read_enable), .Q(MBR_q), .clk(clock_1_out));  // open: clr
  busif busif_3 (
    .Bus_ID(3'b001), .Bus_Write_to_ID(Write_To_ID), .Bus_Read_from_ID(Read_From_ID), .Bus_to_IF(Data_Bus),
    .Reg_to_IF(tiny_bit_extender_1__16b_to_bus), .IF_to_Reg(busif_3_if_to_reg),
    .Read_Enable(busif_3_read_enable), .IF_to_Bus(Data_Bus));
  tiny_bit_extender tiny_bit_extender_1 (
    ._16b_from_bus(busif_3_if_to_reg), ._16b_to_bus(tiny_bit_extender_1__16b_to_bus),
    ._12b_to_reg(tiny_bit_extender_1__12b_to_reg), ._12b_from_reg(MAR_q));
  Register #(.width(12)) MAR (
    .D(tiny_bit_extender_1__12b_to_reg), .en(busif_3_read_enable), .Q(MAR_q), .clk(clock_1_out));  // open: clr
  busif busif_4 (
    .Bus_ID(3'b000), .Bus_Write_to_ID(Write_To_ID), .Bus_Read_from_ID(Read_From_ID), .Bus_to_IF(Data_Bus),
    .Reg_to_IF(ram_1_data), .IF_to_Reg(busif_4_if_to_reg), .Read_Enable(busif_4_read_enable),
    .IF_to_Bus(Data_Bus));
  RAM #(.addrWidth(12), .dataWidth(16), .bus("separate")) ram_1 (
    .addr(MAR_q), .din(busif_4_if_to_reg), .data(ram_1_data), .str(busif_4_read_enable), .clk(clock_1_out));  // open: sel, ld, clr

  // Notes on the sheet:
  //   MARIE Architecture Part 2
  //   Your Name Here
endmodule

module busif (
  input  [15:0] Bus_to_IF,
  input  [2:0] Bus_ID,
  input  [2:0] Bus_Write_to_ID,
  input  [2:0] Bus_Read_from_ID,
  input  [15:0] Reg_to_IF,
  output [15:0] IF_to_Bus,
  output [15:0] IF_to_Reg,
  output Read_Enable
);

  wire comparator_2_eq;

  Comparator #(.width(3)) comparator_1 (.a(Bus_ID), .b(Bus_Write_to_ID), .eq(Read_Enable));  // open: gt, lt
  assign IF_to_Bus = comparator_2_eq ? Reg_to_IF : 16'bz;  // Controlled_Buffer controlled_buffer_1
  Comparator #(.width(3)) comparator_2 (.a(Bus_ID), .b(Bus_Read_from_ID), .eq(comparator_2_eq));  // open: gt, lt

  assign IF_to_Reg = Bus_to_IF;
endmodule

// ALU
module alu (
  input  [15:0] A,
  input  [15:0] B,
  input  [1:0] F,
  output [15:0] Q
);

  wire [15:0] adder_1_out, subtractor_1_out;

  Adder #(.width(16)) adder_1 (.a(A), .b(B), .out(adder_1_out));  // open: cin, cout
  Subtractor #(.width(16)) subtractor_1 (.a(A), .b(B), .out(subtractor_1_out));  // open: bin, bout
  Multiplexer #(.select(2), .width(16), .enable("false")) multiplexer_1 (
    .in0({16{1'b0}}), .in1(subtractor_1_out), .in2(adder_1_out), .in3({16{1'b0}}), .out(Q), .sel(F));
endmodule

// BE
module tiny_bit_extender (
  input  [15:0] _16b_from_bus,
  input  [11:0] _12b_from_reg,
  output [15:0] _16b_to_bus,
  output [11:0] _12b_to_reg
);

  Bit_Extender #(.in_width(16), .out_width(12)) bit_extender_1 (.in(_16b_from_bus), .out(_12b_to_reg));
  assign _16b_to_bus = {{4{1'b0}}, _12b_from_reg};  // Bit_Extender bit_extender_2

  // Notes on the sheet:
  //   This circuit lets us connect a 12-bit register to the 16-bit bus.
  //   It's not strictly neccesary: we could put those two bit extenders
  //   in the main circuit. But, this makes it look neater.
endmodule
