// Logisim project part_3_solution.circ as structural Verilog: 6 circuits, main circuit busif
// ALU
module main (
  input  PC_1,
  input  [1:0] ALU_Func,
  input  [2:0] Write_To_ID,
  input  [2:0] Read_From_ID,
  output [15:0] Data_Bus
);

  wire ac_control_1_ac_enable, busif_1_read_enable, busif_2_read_enable, busif_3_read_enable,
       busif_4_read_enable, busif_5_read_enable, busif_6_read_enable, busif_7_read_enable,
       busif_8_read_enable, clock_1_out;
  wire [11:0] MAR_q, pc_1_q, tiny_bit_extender_1__12b_to_reg, tiny_bit_extender_2__12b_to_reg;
  wire [15:0] ac_control_1_ac_data, AC_q, alu_1_q, busif_1_if_to_reg, busif_2_if_to_reg, busif_3_if_to_reg,
       busif_4_if_to_reg, busif_5_if_to_reg, busif_6_if_to_reg, busif_7_if_to_reg, busif_8_if_to_reg, IN_q,
       IR_q, MBR_q, OUT_q, ram_1_data, tiny_bit_extender_1__16b_to_bus, tiny_bit_extender_2__16b_to_bus;

  busif busif_1 (
    .Bus_ID(3'b111), .Bus_Write_to_ID(Write_To_ID), .Bus_Read_from_ID(Read_From_ID), .Bus_to_IF(Data_Bus),
    .Reg_to_IF(IR_q), .IF_to_Reg(busif_1_if_to_reg), .Read_Enable(busif_1_read_enable), .IF_to_Bus(Data_Bus));
  Clock clock_1 (.out(clock_1_out));
  Register #(.width(16)) IR (
    .D(busif_1_if_to_reg), .en(busif_1_read_enable), .Q(IR_q), .clk(clock_1_out));  // open: clr
  busif busif_2 (
    .Bus_ID(3'b110), .Bus_Write_to_ID(Write_To_ID), .Bus_Read_from_ID(Read_From_ID), .Bus_to_IF(Data_Bus),
    .Reg_to_IF(OUT_q), .IF_to_Reg(busif_2_if_to_reg), .Read_Enable(busif_2_read_enable), .IF_to_Bus(Data_Bus));
  Register #(.width(16)) OUT (
    .D(busif_2_if_to_reg), .en(busif_2_read_enable), .Q(OUT_q), .clk(clock_1_out));  // open: clr
  busif busif_3 (
    .Bus_ID(3'b101), .Bus_Write_to_ID(Write_To_ID), .Bus_Read_from_ID(Read_From_ID), .Bus_to_IF(Data_Bus),
    .Reg_to_IF(IN_q), .IF_to_Reg(busif_3_if_to_reg), .Read_Enable(busif_3_read_enable), .IF_to_Bus(Data_Bus));
  Register #(.width(16)) IN (
    .D(busif_3_if_to_reg), .en(busif_3_read_enable), .Q(IN_q), .clk(clock_1_out));  // open: clr
  busif busif_4 (
    .Bus_ID(3'b100), .Bus_Write_to_ID(Write_To_ID), .Bus_Read_from_ID(Read_From_ID), .Bus_to_IF(Data_Bus),
    .Reg_to_IF(AC_q), .IF_to_Reg(busif_4_if_to_reg), .Read_Enable(busif_4_read_enable), .IF_to_Bus(Data_Bus));
  alu alu_1 (.A(MBR_q), .B(AC_q), .Q(alu_1_q), .F(ALU_Func));
  ac_control ac_control_1 (
    .Bus_Data(busif_4_if_to_reg), .ALU_Result(alu_1_q), .ALU_Function(ALU_Func),
    .Bus_Read(busif_4_read_enable), .AC_Data(ac_control_1_ac_data), .AC_Enable(ac_control_1_ac_enable));
  busif busif_5 (
    .Bus_ID(3'b011), .Bus_Write_to_ID(Write_To_ID), .Bus_Read_from_ID(Read_From_ID), .Bus_to_IF(Data_Bus),
    .Reg_to_IF(MBR_q), .IF_to_Reg(busif_5_if_to_reg), .Read_Enable(busif_5_read_enable), .IF_to_Bus(Data_Bus));
  Register #(.width(16)) AC (
    .D(ac_control_1_ac_data), .en(ac_control_1_ac_enable), .Q(AC_q), .clk(clock_1_out));  // open: clr
  busif busif_6 (
    .Bus_ID(3'b010), .Bus_Write_to_ID(Write_To_ID), .Bus_Read_from_ID(Read_From_ID), .Bus_to_IF(Data_Bus),
    .Reg_to_IF(tiny_bit_extender_1__16b_to_bus), .IF_to_Reg(busif_6_if_to_reg),
    .Read_Enable(busif_6_read_enable), .IF_to_Bus(Data_Bus));
  Register #(.width(16)) MBR (
    .D(busif_5_if_to_reg), .en(busif_5_read_enable), .Q(MBR_q), .clk(clock_1_out));  // open: clr
  tiny_bit_extender tiny_bit_extender_1 (
    ._16b_from_bus(busif_6_if_to_reg), ._16b_to_bus(tiny_bit_extender_1__16b_to_bus),
    ._12b_to_reg(tiny_bit_extender_1__12b_to_reg), ._12b_from_reg(pc_1_q));
  pc u_pc_1 (
    .Q(pc_1_q), .D(tiny_bit_extender_1__12b_to_reg), .en(busif_6_read_enable), .clock(clock_1_out), .inc(PC_1));
  // Probe on pc_1_q
  busif busif_7 (
    .Bus_ID(3'b001), .Bus_Write_to_ID(Write_To_ID), .Bus_Read_from_ID(Read_From_ID), .Bus_to_IF(Data_Bus),
    .Reg_to_IF(tiny_bit_extender_2__16b_to_bus), .IF_to_Reg(busif_7_if_to_reg),
    .Read_Enable(busif_7_read_enable), .IF_to_Bus(Data_Bus));
  tiny_bit_extender tiny_bit_extender_2 (
    ._16b_from_bus(busif_7_if_to_reg), ._16b_to_bus(tiny_bit_extender_2__16b_to_bus),
    ._12b_to_reg(tiny_bit_extender_2__12b_to_reg), ._12b_from_reg(MAR_q));
  Register #(.width(12)) MAR (
    .D(tiny_bit_extender_2__12b_to_reg), .en(busif_7_read_enable), .Q(MAR_q), .clk(clock_1_out));  // open: clr
  busif busif_8 (
    .Bus_ID(3'b000), .Bus_Write_to_ID(Write_To_ID), .Bus_Read_from_ID(Read_From_ID), .Bus_to_IF(Data_Bus),
    .Reg_to_IF(ram_1_data), .IF_to_Reg(busif_8_if_to_reg), .Read_Enable(busif_8_read_enable),
    .IF_to_Bus(Data_Bus));
  RAM #(.addrWidth(12), .dataWidth(16), .bus("separate")) ram_1 (
    .addr(MAR_q), .din(busif_8_if_to_reg), .data(ram_1_data), .str(busif_8_read_enable), .clk(clock_1_out));  // open: sel, ld, clr

  // Notes on the sheet:
  //   MARIE Architecture Part 3
  //   Your Name Here
endmodule

module busif (
  input  [15:0] Bus_to_IF,
  input  [2:0] Bus_ID,
  input  [2:0] Bus_Write_to_ID,
  input  [2:0] Bus_Read_from_ID,
  input  [15:0] Reg_to_IF,
  output [15:0] IF_to_Bus,
  output [15:0] IF_to_Reg,
  output Read_Enable
);

  wire comparator_2_eq;

  Comparator #(.width(3)) comparator_1 (.a(Bus_ID), .b(Bus_Write_to_ID), .eq(Read_Enable));  // open: gt, lt
  assign IF_to_Bus = comparator_2_eq ? Reg_to_IF : 16'bz;  // Controlled_Buffer controlled_buffer_1
  Comparator #(.width(3)) comparator_2 (.a(Bus_ID), .b(Bus_Read_from_ID), .eq(comparator_2_eq));  // open: gt, lt

  assign IF_to_Reg = Bus_to_IF;
endmodule

// ALU
module alu (
  input  [15:0] A,
  input  [15:0] B,
  input  [1:0] F,
  output [15:0] Q
);

  wire [15:0] adder_1_out, subtractor_1_out;

  Adder #(.width(16)) adder_1 (.a(A), .b(B), .out(adder_1_out));  // open: cin, cout
  Subtractor #(.width(16)) subtractor_1 (.a(A), .b(B), .out(subtractor_1_out));  // open: bin, bout
  Multiplexer #(.select(2), .width(16), .enable("false")) multiplexer_1 (
    .in0({16{1'b0}}), .in1(subtractor_1_out), .in2(adder_1_out), .in3({16{1'b0}}), .out(Q), .sel(F));
endmodule

// BE
module tiny_bit_extender (
  input  [15:0] _16b_from_bus,
  input  [11:0] _12b_from_reg,
  output [15:0] _16b_to_bus,
  output [11:0] _12b_to_reg
);

  Bit_Extender #(.in_width(16), .out_width(12)) bit_extender_1 (.in(_16b_from_bus), .out(_12b_to_reg));
  assign _16b_to_bus = {{4{1'b0}}, _12b_from_reg};  // Bit_Extender bit_extender_2

  // Notes on the sheet:
  //   This circuit lets us connect a 12-bit register to the 16-bit bus.
  //   It's not strictly neccesary: we could put those two bit extenders
  //   in the main circuit. But, this makes it look neater.
endmodule

module ac_control (
  input  [15:0] Bus_Data,
  input  [15:0] ALU_Result,
  input  [1:0] ALU_Function,
  input  Bus_Read,
  output [15:0] AC_Data,
  output AC_Enable
);

  wire or_1_out;

  or or_1 (or_1_out, ALU_Function[0], ALU_Function[1]);
  Multiplexer #(.width(16), .enable("false")) multiplexer_1 (
    .in0(Bus_Data), .in1(ALU_Result), .out(AC_Data), .sel(or_1_out));
  or or_2 (AC_Enable, or_1_out, Bus_Read);

  // Notes on the sheet:
  //   If the ALU function isn't 00, it's doing something:
  //   otherwise, the ALU is doing nothing:
  //   the AC should read from the ALU
  //   the AC should be enabled
  //   the AC should read from the bus as normal
  //   the AC should enable from the bus as normal
endmodule

// PC
module pc (
  input  [11:0] D,
  input  en,
  input  clock,
  input  inc,
  output [11:0] Q
);

  wire [11:0] adder_1_out, register_1_q;

  Register #(.width(12)) register_1 (.D(D), .en(en), .Q(register_1_q), .clk(clock));  // open: clr
  Adder #(.width(12)) adder_1 (.a(register_1_q), .b(12'h1), .out(adder_1_out));  // open: cin, cout
  Multiplexer #(.width(12), .enable("false")) multiplexer_1 (.in0(register_1_q), .in1(adder_1_out), .out(Q), .sel(inc));
endmodule
