// Logisim project part_4.circ as structural Verilog: 6 circuits, main circuit busif
// ALU
module main (
  output PC___1,
  output [1:0] ALU_Func,
  output [2:0] Write_To_ID,
  output [2:0] Read_From_ID,
  output [15:0] Data_Bus,
  output [15:0] IR_Output,
  output [15:0] AC_Output
);

  wire busif_1_read_enable, busif_2_read_enable, busif_3_read_enable, busif_4_read_enable,
       busif_5_read_enable, busif_6_read_enable, busif_7_read_enable, busif_8_read_enable, clock_1_out,
       comparator_1_eq, comparator_2_eq, comparator_2_lt, or_1_out;
  wire [11:0] MAR_q, PC_q, tiny_bit_extender_1__12b_to_reg, tiny_bit_extender_2__12b_to_reg;
  wire [15:0] alu_1_q, ALU_COMP_selected_output, busif_1_if_to_reg, busif_2_if_to_reg, busif_3_if_to_reg,
       busif_4_if_to_reg, busif_5_if_to_reg, busif_6_if_to_reg, busif_7_if_to_reg, busif_8_if_to_reg,
       InREG_q, MBR_q, OutREG_q, ram_1_data, tiny_bit_extender_1__16b_to_bus, tiny_bit_extender_2__16b_to_bus;

  control control_1 (
    .AC_Zero(comparator_1_eq), .AC_Negative(or_1_out), .instruction(IR_Output), .Read_From_ID(Read_From_ID),
    .Write_To_ID(Write_To_ID), .ALU_Function(ALU_Func), .PC_1(PC___1));
  Clock clock_1 (.out(clock_1_out));
  or or_1 (or_1_out, comparator_2_eq, comparator_2_lt);
  Comparator #(.width(16)) comparator_1 (.a(AC_Output), .b({16{1'b0}}), .eq(comparator_1_eq));  // open: gt, lt
  Comparator #(.width(16)) comparator_2 (
    .a(AC_Output), .b({16{1'b1}}), .eq(comparator_2_eq), .lt(comparator_2_lt));  // open: gt
  busif busif_1 (
    .Bus_ID(3'b111), .Bus_Write_to_ID(Write_To_ID), .Bus_Read_from_ID(Read_From_ID), .Bus_to_IF(Data_Bus),
    .Reg_to_IF(IR_Output), .IF_to_Reg(busif_1_if_to_reg), .Read_Enable(busif_1_read_enable),
    .IF_to_Bus(Data_Bus));
  busif busif_2 (
    .Bus_ID(3'b110), .Bus_Write_to_ID(Write_To_ID), .Bus_Read_from_ID(Read_From_ID), .Bus_to_IF(Data_Bus),
    .Reg_to_IF(OutREG_q), .IF_to_Reg(busif_2_if_to_reg), .Read_Enable(busif_2_read_enable),
    .IF_to_Bus(Data_Bus));
  Register #(.width(16)) IR (
    .D(busif_1_if_to_reg), .en(busif_1_read_enable), .Q(IR_Output), .clk(clock_1_out));  // open: clr
  Register #(.width(16)) OutREG (
    .D(busif_2_if_to_reg), .en(busif_2_read_enable), .Q(OutREG_q), .clk(clock_1_out));  // open: clr
  busif busif_3 (
    .Bus_ID(3'b101), .Bus_Write_to_ID(Write_To_ID), .Bus_Read_from_ID(Read_From_ID), .Bus_to_IF(Data_Bus),
    .Reg_to_IF(InREG_q), .IF_to_Reg(busif_3_if_to_reg), .Read_Enable(busif_3_read_enable),
    .IF_to_Bus(Data_Bus));
  Register #(.width(16)) InREG (
    .D(busif_3_if_to_reg), .en(busif_3_read_enable), .Q(InREG_q), .clk(clock_1_out));  // open: clr
  alu alu_1 (.A(AC_Output), .B(MBR_q), .Q(alu_1_q), .F(ALU_Func));
  busif busif_4 (
    .Bus_ID(3'b100), .Bus_Write_to_ID(Write_To_ID), .Bus_Read_from_ID(Read_From_ID), .Bus_to_IF(Data_Bus),
    .Reg_to_IF(AC_Output), .IF_to_Reg(busif_4_if_to_reg), .Read_Enable(busif_4_read_enable),
    .IF_to_Bus(Data_Bus));
  ALU_Comparator ALU_COMP (
    .ALU_Control(ALU_Func), .ALU__Input(alu_1_q), .IF_to_REG_Input(busif_4_if_to_reg),
    .SELECTED_Output(ALU_COMP_selected_output));
  busif busif_5 (
    .Bus_ID(3'b011), .Bus_Write_to_ID(Write_To_ID), .Bus_Read_from_ID(Read_From_ID), .Bus_to_IF(Data_Bus),
    .Reg_to_IF(MBR_q), .IF_to_Reg(busif_5_if_to_reg), .Read_Enable(busif_5_read_enable), .IF_to_Bus(Data_Bus));
  Register #(.width(16)) AC (
    .D(ALU_COMP_selected_output), .en(busif_4_read_enable), .Q(AC_Output), .clk(clock_1_out));  // open: clr
  Register #(.width(16)) MBR (
    .D(busif_5_if_to_reg), .en(busif_5_read_enable), .Q(MBR_q), .clk(clock_1_out));  // open: clr
  busif busif_6 (
    .Bus_ID(3'b010), .Bus_Write_to_ID(Write_To_ID), .Bus_Read_from_ID(Read_From_ID), .Bus_to_IF(Data_Bus),
    .Reg_to_IF(tiny_bit_extender_1__16b_to_bus), .IF_to_Reg(busif_6_if_to_reg),
    .Read_Enable(busif_6_read_enable), .IF_to_Bus(Data_Bus));
  tiny_bit_extender tiny_bit_extender_1 (
    ._16b_from_bus(busif_6_if_to_reg), ._16b_to_bus(tiny_bit_extender_1__16b_to_bus),
    ._12b_to_reg(tiny_bit_extender_1__12b_to_reg), ._12b_from_reg(PC_q));
  pc PC (
    .Increment(PC___1), .D(tiny_bit_extender_1__12b_to_reg), .Enable(busif_6_read_enable),
    .Clock(clock_1_out), .Q(PC_q));
  busif busif_7 (
    .Bus_ID(3'b001), .Bus_Write_to_ID(Write_To_ID), .Bus_Read_from_ID(Read_From_ID), .Bus_to_IF(Data_Bus),
    .Reg_to_IF(tiny_bit_extender_2__16b_to_bus), .IF_to_Reg(busif_7_if_to_reg),
    .Read_Enable(busif_7_read_enable), .IF_to_Bus(Data_Bus));
  tiny_bit_extender tiny_bit_extender_2 (
    ._16b_from_bus(busif_7_if_to_reg), ._16b_to_bus(tiny_bit_extender_2__16b_to_bus),
    ._12b_to_reg(tiny_bit_extender_2__12b_to_reg), ._12b_from_reg(MAR_q));
  // Probe on PC_q
  Register #(.width(12)) MAR (
    .D(tiny_bit_extender_2__12b_to_reg), .en(busif_7_read_enable), .Q(MAR_q), .clk(clock_1_out));  // open: clr
  busif busif_8 (
    .Bus_ID(3'b000), .Bus_Write_to_ID(Write_To_ID), .Bus_Read_from_ID(Read_From_ID), .Bus_to_IF(Data_Bus),
    .Reg_to_IF(ram_1_data), .IF_to_Reg(busif_8_if_to_reg), .Read_Enable(busif_8_read_enable),
    .IF_to_Bus(Data_Bus));
  RAM #(.addrWidth(12), .dataWidth(16), .bus("separate")) ram_1 (
    .addr(MAR_q), .din(busif_8_if_to_reg), .data(ram_1_data), .str(busif_8_read_enable), .clk(clock_1_out));  // open: sel, ld, clr

  // Notes on the sheet:
  //   PC+1
  //   ALU
  //   Write
  //   Read
  //   Instruction
  //   AC Negative
  //   AC Zero
  //   MARIE Architecture Part 4
  //   Dustin Meckley
endmodule

module busif (
  input  [15:0] Bus_to_IF,
  input  [2:0] Bus_ID,
  input  [2:0] Bus_Write_to_ID,
  input  [2:0] Bus_Read_from_ID,
  input  [15:0] Reg_to_IF,
  output [15:0] IF_to_Bus,
  output [15:0] IF_to_Reg,
  output Read_Enable
);

  wire comparator_2_eq;

  Comparator #(.width(3)) comparator_1 (.a(Bus_ID), .b(Bus_Write_to_ID), .eq(Read_Enable));  // open: gt, lt
  assign IF_to_Bus = comparator_2_eq ? Reg_to_IF : 16'bz;  // Controlled_Buffer controlled_buffer_1
  Comparator #(.width(3)) comparator_2 (.a(Bus_ID), .b(Bus_Read_from_ID), .eq(comparator_2_eq));  // open: gt, lt

  assign IF_to_Reg = Bus_to_IF;
endmodule

// BE
module tiny_bit_extender (
  input  [15:0] _16b_from_bus,
  input  [11:0] _12b_from_reg,
  output [15:0] _16b_to_bus,
  output [11:0] _12b_to_reg
);

  Bit_Extender #(.in_width(16), .out_width(12)) bit_extender_1 (.in(_16b_from_bus), .out(_12b_to_reg));
  assign _16b_to_bus = {{4{1'b0}}, _12b_from_reg};  // Bit_Extender bit_extender_2

  // Notes on the sheet:
  //   This circuit lets us connect a 12-bit register to the 16-bit bus.
  //   It's not strictly neccesary: we could put those two bit extenders
  //   in the main circuit. But, this makes it look neater.
endmodule

// ALU
module alu (
  input  [15:0] A,
  input  [15:0] B,
  input  [1:0] F,
  output [15:0] Q
);

  wire [15:0] adder_1_out, subtractor_1_out;

  Adder #(.width(16)) adder_1 (.a(A), .b(B), .out(adder_1_out));  // open: cin, cout
  Subtractor #(.width(16)) subtractor_1 (.a(A), .b(B), .out(subtractor_1_out));  // open: bin, bout
  Multiplexer #(.select(2), .width(16), .enable("false")) multiplexer_1 (
    .in0({16{1'b0}}), .in1(adder_1_out), .in2(subtractor_1_out), .in3({16{1'b0}}), .out(Q), .sel(F));
endmodule

module ALU_Comparator (
  input  [1:0] ALU_Control,
  input  [15:0] ALU__Input,
  input  [15:0] IF_to_REG_Input,
  output [15:0] SELECTED_Output
);

  wire comparator_1_eq;

  Comparator #(.width(2)) comparator_1 (.a(ALU_Control), .b(2'b00), .eq(comparator_1_eq));  // open: gt, lt
  Multiplexer #(.width(16), .enable("false")) multiplexer_1 (
    .in0(ALU__Input), .in1(IF_to_REG_Input), .out(SELECTED_Output), .sel(comparator_1_eq));
endmodule

module pc (
  input  Increment,
  input  [11:0] D,
  input  Enable,
  input  Clock,
  output [11:0] Q
);

  wire [11:0] adder_1_out, multiplexer_1_out;

  Adder #(.width(12)) adder_1 (.a(D), .b(12'h1), .out(adder_1_out));  // open: cin, cout
  Multiplexer #(.width(12), .enable("false")) multiplexer_1 (
    .in0(D), .in1(adder_1_out), .out(multiplexer_1_out), .sel(Increment));
  Register #(.width(12)) register_1 (.D(multiplexer_1_out), .en(Enable), .Q(Q), .clk(Clock));  // open: clr
endmodule
